# Fritzing sketch dam_controller (saved by Fritzing 0.9.3b)
breadboards: 1

parts:
  Componente1 = Bluetooth HC-05 Macho
  Componente2 = Arduino Uno (Rev3)
  LED1 = LED - 5mm [color="Green (570nm)" package="5 mm [THT]"]
  R1 = Resistor [tolerance=±5% resistance=220 package="2512 [SMD]"]
  J1 = Basic Servo

nets:
  N1: Componente1.TXD, Componente2.D2
  N2: Componente1.RXD, Componente2.D3_PWM
  VCC: Componente1.VCC, Componente2.5V, J1.vcc
  GND: Componente1.GND, Componente2.GND, LED1.cathode, J1.gnd
  N3: Componente2.D13/SCK, R1.Pin_1
  N4: Componente2.D7, J1.pulse
  N5: LED1.anode, R1.Pin_0
