# Fritzing sketch dam_remote_hydrometer (saved by Fritzing 0.9.3b)
breadboards: 1

parts:
  hc-sr1 = hc-sr04  # not connected
  LED1 = LED - 5mm [color="Red (633nm)" package="5 mm [THT]"]  # not connected
  Amica_NodeMCU_DevKit_1_1 = Amica NodeMCU DevKit 1.0

nets:
  N1: Amica_NodeMCU_DevKit_1_1.pin1, Amica_NodeMCU_DevKit_1_1.pin_9, Amica_NodeMCU_DevKit_1_1.pin_10, Amica_NodeMCU_DevKit_1_1.pin_23, Amica_NodeMCU_DevKit_1_1.pin_24, Amica_NodeMCU_DevKit_1_1.pin_25, Amica_NodeMCU_DevKit_1_1.pin_26, Amica_NodeMCU_DevKit_1_1.pin_27, Amica_NodeMCU_DevKit_1_1.pin_29, Amica_NodeMCU_DevKit_1_1.pin_30
  N2: Amica_NodeMCU_DevKit_1_1.pin4, Amica_NodeMCU_DevKit_1_1.pin5, Amica_NodeMCU_DevKit_1_1.pin6, Amica_NodeMCU_DevKit_1_1.pin7, Amica_NodeMCU_DevKit_1_1.pin8
  N3: Amica_NodeMCU_DevKit_1_1.pin_11, Amica_NodeMCU_DevKit_1_1.pin_12, Amica_NodeMCU_DevKit_1_1.pin_13, Amica_NodeMCU_DevKit_1_1.pin_14, Amica_NodeMCU_DevKit_1_1.pin_15
  N4: Amica_NodeMCU_DevKit_1_1.pin_16, Amica_NodeMCU_DevKit_1_1.pin_17, Amica_NodeMCU_DevKit_1_1.pin_18, Amica_NodeMCU_DevKit_1_1.pin_19, Amica_NodeMCU_DevKit_1_1.pin_20

custom parts:
  Amica NodeMCU DevKit 1.0: Amica NodeMCU DEVKIT 1.0 Development Kit based on ESP8266 ESP-12E, integating GPIO, PWM, IIC, 1-Wire and ADC all in one board.
