# Fritzing sketch smart_exp_circuit (saved by Fritzing 0.9.3b)
breadboards: 2

parts:
  Componente1 = Arduino Uno (Rev3)
  R1 = Rotary Potentiometer (Small) [maximum_resistance=100kΩ package=THT]
  Led2 = LED - 5mm [color="Red (633nm)" package="5 mm [THT]"]
  Led1 = LED - 5mm [color="Green (560nm)" package="5 mm [THT]"]
  ButtonStart = Pushbutton [package="[THT]"]
  ButtonStop = Pushbutton [package="[THT]"]
  hc-sr1 = hc-sr04
  R2 = Resistor [tolerance=±5% resistance=220 package=THT]
  R3 = Resistor [tolerance=±5% resistance=220 package=THT]
  R4 = Resistor [tolerance=±5% resistance=10k package=THT]
  R5 = Resistor [tolerance=±5% resistance=10k package=THT]
  Componente2 = HC-SR501 Body Sensor Module
  DHT1 = DHT11 Humitidy and Temperature Sensor (3 pins)
  J2 = Basic Servo

nets:
  N1: Componente1.A0, R1.wiper
  N2: Componente1.D9_PWM, ButtonStart.Pin_3, ButtonStart.Pin_4, R5.Pin_1
  N3: Componente1.D10_PWM/SS, ButtonStop.Pin_3, ButtonStop.Pin_4, R4.Pin_1
  N4: Componente1.D12/MISO, R2.Pin_1
  N5: Componente1.D13/SCK, R3.Pin_1
  N6: Componente1.D2, Componente2.OUT
  N7: Componente1.D4, hc-sr1.Echo
  N8: Componente1.D5_PWM, DHT1.DATA
  N9: Componente1.D6_PWM, hc-sr1.Trig
  N10: Componente1.D7, J2.pulse
  VCC: Componente1.5V, R1.leg1, ButtonStart.Pin_1, ButtonStart.Pin_2, ButtonStop.Pin_1, ButtonStop.Pin_2, hc-sr1.VCC, Componente2.VCC, DHT1.VDD, J2.vcc
  GND: Componente1.GND, R1.leg2, Led2.cathode, Led1.cathode, hc-sr1.GND, R4.Pin_0, R5.Pin_0, Componente2.GND, DHT1.GND, J2.gnd
  N11: Led2.anode, R3.Pin_0
  N12: Led1.anode, R2.Pin_0

custom parts:
  HC-SR501 Body Sensor Module: Pyroelectric Infrared PIR Motion Sensor Detector Module
  DHT11 Humitidy and Temperature Sensor (3 pins): DHT11 Humidity and Temperature Sensor (3 pins) from the design created by John De Cristofaro for Adafruit Industries.
