# Fritzing sketch track_the_led_fly (saved by Fritzing 0.9.3b)
breadboards: 1

parts:
  S6 = Pushbutton [package="[THT]"]
  S7 = Pushbutton [package="[THT]"]
  S8 = Pushbutton [package="[THT]"]
  S9 = Pushbutton [package="[THT]"]
  R12 = Resistor [tolerance=±5% resistance=10k package=THT]
  R13 = Resistor [tolerance=±5% resistance=10k package=THT]
  R14 = Resistor [tolerance=±5% resistance=10k package=THT]
  R15 = Resistor [tolerance=±5% resistance=10k package=THT]
  R16 = Rotary Potentiometer (Small) [maximum_resistance=100kΩ package=THT]
  Part2 = Arduino Uno (Rev3)
  R17 = Resistor [tolerance=±5% resistance=220 package=THT]
  R18 = Resistor [tolerance=±5% resistance=220 package=THT]
  R19 = Resistor [tolerance=±5% resistance=220 package=THT]
  R20 = Resistor [tolerance=±5% resistance=220 package=THT]
  LED7 = LED - 5mm [color="Green (555nm)" package="5 mm [THT]"]
  LED8 = LED - 5mm [color="Green (555nm)" package="5 mm [THT]"]
  LED9 = LED - 5mm [color="Green (555nm)" package="5 mm [THT]"]
  LED10 = LED - 5mm [color="Green (555nm)" package="5 mm [THT]"]
  R21 = Resistor [tolerance=±5% resistance=220 package=THT]
  LED11 = LED - 5mm [color="Red (633nm)" package="5 mm [THT]"]

nets:
  N1: S6.Pin_1, S6.Pin_2, R12.Pin_0, Part2.D2
  N2: S6.Pin_3, S6.Pin_4, S7.Pin_3, S7.Pin_4, S8.Pin_3, S8.Pin_4, S9.Pin_3, S9.Pin_4, R16.leg1, Part2.5V
  N3: S7.Pin_1, S7.Pin_2, R13.Pin_0, Part2.D3_PWM
  N4: S8.Pin_1, S8.Pin_2, R14.Pin_0, Part2.D4
  N5: S9.Pin_1, S9.Pin_2, R15.Pin_0, Part2.D5_PWM
  N6: R12.Pin_1, R13.Pin_1, R14.Pin_1, R15.Pin_1, R16.leg2, Part2.GND, LED7.cathode, LED8.cathode, LED9.cathode, LED10.cathode, LED11.cathode
  N7: R16.wiper, Part2.A0
  N8: Part2.D10_PWM/SS, R17.Pin_0
  N9: Part2.D11_PWM/MOSI, R18.Pin_0
  N10: Part2.D12/MISO, R19.Pin_0
  N11: Part2.D13/SCK, R20.Pin_0
  N12: Part2.D7, R21.Pin_0
  N13: R17.Pin_1, LED7.anode
  N14: R18.Pin_1, LED8.anode
  N15: R19.Pin_1, LED9.anode
  N16: R20.Pin_1, LED10.anode
  N17: R21.Pin_1, LED11.anode
