# Fritzing sketch track_the_led_fly1 (saved by Fritzing 0.9.5d)
breadboards: 1

parts:
  S2 = Pushbutton [package="[THT]"]
  R3 = Resistor [tolerance=±5% resistance=10k package=THT]
  R4 = Resistor [tolerance=±5% resistance=220 package=THT]
  LED2 = LED - 5mm [color="Green (555nm)" package="5 mm [THT]"]
  S3 = Pushbutton [package="[THT]"]
  R5 = Resistor [tolerance=±5% resistance=10k package=THT]
  R6 = Resistor [tolerance=±5% resistance=220 package=THT]
  LED3 = LED - 5mm [color="Green (555nm)" package="5 mm [THT]"]
  S4 = Pushbutton [package="[THT]"]
  R7 = Resistor [tolerance=±5% resistance=10k package=THT]
  R8 = Resistor [tolerance=±5% resistance=220 package=THT]
  LED4 = LED - 5mm [color="Green (555nm)" package="5 mm [THT]"]
  S5 = Pushbutton [package="[THT]"]
  R9 = Resistor [tolerance=±5% resistance=10k package=THT]
  R10 = Resistor [tolerance=±5% resistance=220 package=THT]
  LED5 = LED - 5mm [color="Green (555nm)" package="5 mm [THT]"]
  R11 = Rotary Potentiometer (Small) [maximum_resistance=100kΩ package=THT]
  R12 = Resistor [tolerance=±5% resistance=220 package=THT]
  LED6 = LED - 5mm [color="Red (633nm)" package="5 mm [THT]"]
  Part1 = Arduino Uno (Rev3)

nets:
  N1: S2.Pin_1, S2.Pin_2, R3.Pin_0, Part1.D8
  N2: S2.Pin_3, S2.Pin_4, R4.Pin_0, S3.Pin_3, S3.Pin_4, R6.Pin_0, S4.Pin_3, S4.Pin_4, R8.Pin_0, S5.Pin_3, S5.Pin_4, R10.Pin_0, R11.leg1, Part1.D10_PWM/SS, Part1.D11_PWM/MOSI, Part1.D12/MISO, Part1.D13/SCK, Part1.5V
  N3: R3.Pin_1, LED2.cathode, R5.Pin_1, LED3.cathode, R7.Pin_1, LED4.cathode, R9.Pin_1, LED5.cathode, R11.leg2, LED6.cathode, Part1.GND
  N4: R4.Pin_1, LED2.anode
  N5: S3.Pin_1, S3.Pin_2, R5.Pin_0, Part1.D7
  N6: R6.Pin_1, LED3.anode
  N7: S4.Pin_1, S4.Pin_2, R7.Pin_0, Part1.D6_PWM
  N8: R8.Pin_1, LED4.anode
  N9: S5.Pin_1, S5.Pin_2, R9.Pin_0, Part1.D5_PWM
  N10: R10.Pin_1, LED5.anode
  N11: R11.wiper, Part1.A0
  N12: R12.Pin_0, Part1.D3_PWM
  N13: R12.Pin_1, LED6.anode
